# Fritzing sketch schematics (saved by Fritzing 1.0.6)
stripboards: 1
breadboards: 1

parts:
  R1 = Resistor [tolerance=±5% power=0.25W resistance=220 package=THT]
  R2 = Resistor [tolerance=±5% power=0.25W resistance=220 package=THT]
  R3 = Resistor [tolerance=±5% power=0.25W resistance=220 package=THT]
  Switch1 = Pushbutton [package="[THT]"]
  Switch2 = Pushbutton [package="[THT]"]
  R4 = Rotary Potentiometer (Small) [maximum_resistance=4.7kΩ knob_status=50% power=0.5W package=THT]
  R4_2 = Resistor [tolerance=±5% power=0.25W resistance=4.7k package=THT]
  V2 = DC Power Supply [voltage=5V internal_resistance=1Ω max_current=0.1A]
  U1 = attiny85 [package=dip]
  C1 = Ceramic Capacitor [capacitance=100nF voltage=35V package="100 mil [THT, multilayer]"]
  R6 = Resistor [tolerance=±5% power=0.25W resistance=10k package=THT]
  LED1 = LED - 3mm [color="Green (560nm)" current=0.030A package="3 mm [THT]"]
  LED2 = LED - 3mm [color="Yellow (592nm)" current=0.030A package="3 mm [THT]"]
  LED3 = LED - 3mm [color="Red (633nm)" current=0.030A package="3 mm [THT]"]
  R5 = Resistor [tolerance=±5% power=0.25W resistance=4.7k package=THT]

nets:
  N1: R1.Pin_0, U1.Pin_2
  N2: R1.Pin_1, LED1.anode
  N3: R2.Pin_0, U1.Pin_5
  N4: R2.Pin_1, LED2.anode
  N5: R3.Pin_0, U1.Pin_6
  N6: R3.Pin_1, LED3.anode
  N7: Switch1.Pin_1, Switch1.Pin_2, Switch2.Pin_1, Switch2.Pin_2, R4.leg1, V2.Pin_1, U1.Pin_4, C1.0, LED1.cathode, LED2.cathode, LED3.cathode
  N8: Switch1.Pin_3, Switch1.Pin_4, U1.Pin_3, R5.Pin_0
  N9: Switch2.Pin_3, Switch2.Pin_4, R4_2.Pin_0
  N10: R4.wiper, U1.Pin_7
  N11: R4.leg2, R4_2.Pin_1, V2.Pin_2, U1.Pin_8, C1.1, R6.Pin_0, R5.Pin_1
  N12: U1.Pin_1, R6.Pin_1
